# Fritzing sketch Doorbell (saved by Fritzing 0.9.3b)
circuit board: 4cm x 6cm
breadboards: 1

parts:
  Part1 = Arduino Pro Mini v13
  U2 = V_REG_LD1117VXX [package=78xxl]
  Part2 = NRF24L01+ Breakout Board
  C1 = Electrolytic Capacitor [capacitance=100μF package="0807 [SMD, electrolytic]"]
  Q1 = MOSFET-NCHANNEL [package=to220v]
  R1 = Resistor [tolerance=±5% resistance=220 package="1206 [SMD]"]
  L1 = Solenoid
  J1 = Power Jack [package=power_jack_pth_lock]

nets:
  VCC: Part1.VCC, U2.OUT, Part2.VCC, C1.+
  GND: Part1.GND, U2.GND, Part2.GND, C1.-, Q1.S, R1.Pin_0, J1.GND
  N1: Part1.D13/SCK, Part2.SCK
  N2: Part1.D12/MISO, Part2.MISO
  N3: Part1.D11_PWM/MOSI, Part2.MOSI
  N4: Part1.D10_PWM/SS, Part2.CS
  N5: Part1.D9_PWM, Part2.CE
  N6: Part1.D3_PWM, Q1.G, R1.Pin_1
  N7: U2.IN, L1.pin2, J1.PWR
  N8: Q1.D, L1.pin1

// code stored in the sketch: Doorbell.ino
// Enable debug prints to serial monitor
#define MY_DEBUG 

// Enable and select radio type attached
#define MY_RADIO_NRF24
//#define MY_RADIO_RFM69

#include <SPI.h>
#include <MySensors.h>  

#define CHILD_ID 99   // Id of the sensor child

const int BUTTON_PIN = 2;
const int RINGER_PIN = 3;

int buttonState;
int lastButtonState = LOW;
unsigned long lastDebounceTime = 0;
unsigned long debounceDelay = 50;

MyMessage ringerMsg(CHILD_ID, V_STATUS);

boolean ringerStatus;

void setup() {
  Serial.begin(115200);
  pinMode(BUTTON_PIN, INPUT);
  pinMode(RINGER_PIN, OUTPUT);

  ringerStatus = loadState(0);    // Read last lock status from eeprom
  setRingerState(ringerStatus, true); // Now set the last known state and send it to controller
}

void presentation()  {
  sendSketchInfo("Doorbell", "1.0");
  present(CHILD_ID, V_STATUS);
}

void setRingerState(bool state, bool doSend) {
  if (state) 
     Serial.println("Ringer enabled");
  else
     Serial.println("Ringer disabled");
  if (doSend)
    send(ringerMsg.set(state));
}

void loop() {
  int reading = digitalRead(BUTTON_PIN);
  if (reading != lastButtonState) {
    lastDebounceTime = millis();
  }

  if ((millis() - lastDebounceTime) > debounceDelay) {
    if (reading != buttonState) {
      buttonState = reading;
      if (buttonState == HIGH) {
        if (ringerStatus)
          ring();
      }
    }
  }
  lastButtonState = reading;
}

void ring() {
  for (int i=0; i <= 25; i++){
    digitalWrite(RINGER_PIN, HIGH);
    delay(50); 
    digitalWrite(RINGER_PIN, LOW);
    delay(50);
  }
}

void receive(const MyMessage &message) {
  // We only expect one type of message from controller. But we better check anyway.
  if (message.type==V_STATUS) {
     // Change relay state
     setRingerState(message.getBool(), false); 
  
     // Write some debug info
     Serial.print("Incoming ringer status:");
     Serial.println(message.getBool());
   } 
}
